# Fritzing sketch BusArrivingProject (saved by Fritzing 0.9.3b)
breadboards: 1

parts:
  Componente1 = Arduino Uno (Rev3)
  WeMos_D1_Mini1 = WeMos D1 Mini
  LCD1 = LCD screen
  R1 = Rotary Potentiometer (Large) [maximum_resistance=100kΩ package=THT]
  S1 = Momentary Switch [package=ksa_sealed_tac_switch]
  J1 = Piezo Speaker

nets:
  N1: Componente1.D8, LCD1.DB7
  N2: Componente1.D10_PWM/SS, S1.2
  N3: Componente1.D11_PWM/MOSI, WeMos_D1_Mini1.RX
  N4: Componente1.D12/MISO, J1.pin2
  GND: Componente1.GND, WeMos_D1_Mini1.G, LCD1.VSS, LCD1.R/W, LCD1.LED-, R1.leg2, S1.4, J1.pin1
  N5: Componente1.D2, WeMos_D1_Mini1.TX
  N6: Componente1.D3_PWM, LCD1.DB6
  N7: Componente1.D4, LCD1.DB5
  N8: Componente1.D5_PWM, LCD1.DB4
  N9: Componente1.D6_PWM, LCD1.E
  N10: Componente1.D7, LCD1.RS
  5V: Componente1.5V, LCD1.VDD, LCD1.LED+, R1.leg1
  N11: LCD1.V0, R1.wiper
